# Fritzing sketch Midterm2Fritzing (saved by Fritzing 1.0.4)
breadboards: 1

parts:
  SENS1 = SoilWatch 10
  OLED_I2C1 = OLED 128x64 I2C Monochrome Display
  Part1 = MQ-131 breakout
  A1 = Particle - Photon2
  M1 = BMP280
  Relay1 = Relay - 6 pins [package="DIP (Dual Inline) [THT]"]
  WATER_PUMP1 = water pump/motor  # not connected
  Part2 = 12 NeoPixel Ring [part_number=1643]
  Q1 = TRANSISTOR_PNP [package=to-92]
  R1 = Resistor [tolerance=±5% power=0.25W resistance=220 package=THT]
  R2 = Resistor [tolerance=±5% power=0.25W resistance=2.2k package=THT]
  R3 = Resistor [tolerance=±5% power=0.25W resistance=3.3k package=THT]
  R4 = Resistor [tolerance=±5% power=0.25W resistance=1.5k package=THT]
  Q2 = PNP-Transistor [package="TO92 [THT]"]

nets:
  VCC: SENS1.VCC, Part1.DO, A1.Pin_26, Relay1.ON, Part2.VDD, R1.Pin_0, R4.Pin_0
  N1: SENS1.OUT, A1.Pin_5
  GND: SENS1.GND, OLED_I2C1.GND, Part1.AO, A1.Pin_4, A1.Pin_30, A1.Pin_35, M1.GND, Relay1.GND, Part2.GND, Q1.C, R2.Pin_0, Q2.E
  N2: OLED_I2C1.SDA, A1.Pin_17, M1.SDA
  N3: OLED_I2C1.SCK, A1.Pin_18, M1.SCL
  VDD: OLED_I2C1.VDD, A1.Pin_2, A1.Pin_31, M1.VIN, Relay1.VCC
  N4: Part1.VCC, A1.Pin_6
  N5: A1.Pin_13, Q1.B, R2.Pin_1
  N6: A1.Pin_19, R3.Pin_0
  N7: Relay1.IN, Q1.E, R1.Pin_1
  N8: Part2.IN, R4.Pin_1, Q2.C
  N9: R3.Pin_1, Q2.B

custom parts:
  SoilWatch 10: SoilWatch 10 - Capacitive soil moisture sensor
  MQ-131 breakout: SKU: 101282
  Particle - Photon2: The Photon 2 is a microcontroller and Wi-Fi networking developed by particle. Features: 802.11a/b/g/n Wi-Fi, 2.4 GHz and 5 GHz Integrated PCB antenna Integrated U.FL connector for external antenna Integrated RF switch BLE 5 using same antenna as Wi-Fi Realtek RTL8721DM MCU ARM Cortex M33 CPU, 200 MHz 2048 KB (2 MB) user application maximum size 3072 KB (3 MB) of RAM available to user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
  BMP280: Temperature Humidity Barometric presure Sensor, I2C
  Relay - 6 pins: A DIP stand-in part for whatever IC you want. With 6 pins on a 900mil dual inline package (DIP) footprint.
  water pump/motor: WATER PUMP BY ARDUBLOCKTR
  12 NeoPixel Ring: 12 ultra bright smart LED NeoPixels are arranged in a circle with 1.5" (37mm) outer diameter. The rings are 'chainable' - connect the output pin of one to the input pin of another. Use only one microcontroller pin to control as many as you can chain together! Each LED is addressable as the driver chip is inside the LED. Each one has ~18mA constant current drive so the color will be very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
